// Logisim project DataPath.circ as structural Verilog: 2 circuits, main circuit main
module main (
);

  wire alu_1_p4, ALUSrcA, and_1_out, Branch, Clk, IorD, IRWrite, MemtoReg, or_1_out, PCSrc, PCWrite, R_W,
       RegDst;
  wire [1:0] ALUSrcB;
  wire [3:0] ALUControl;
  wire [4:0] multiplexer_2_out;
  wire [31:0] A_q, alu_1_p5, ALUOut_q, B_q, bit_extender_1_out, Data_q, Instr_q, instruction_memory_1_out_4,
       main_1_output, main_2_a, main_2_b, multiplexer_1_out, multiplexer_3_out, multiplexer_4_out,
       multiplexer_5_out, multiplexer_6_out, shifter_1_out;

  PC_main main_1 (.Input(multiplexer_6_out), .Enable(or_1_out), .Clk(Clk), .Output(main_1_output));  // open: Reset
  Multiplexer #(.width(32)) multiplexer_1 (
    .in0(main_1_output), .in1(ALUOut_q), .out(multiplexer_1_out), .sel(IorD));  // open: en
  Instruction_Memory instruction_memory_1 (
    .in_2(multiplexer_1_out), .in_1(Clk), .in_3(B_q), .out_4(instruction_memory_1_out_4));
  Register #(.width(32)) Instr (.D(instruction_memory_1_out_4), .en(IRWrite), .Q(Instr_q), .clk(Clk));  // open: clr
  Register #(.width(32)) Data (.D(instruction_memory_1_out_4), .Q(Data_q), .clk(Clk));  // open: en, clr
  Multiplexer #(.width(5)) multiplexer_2 (
    .in0(Instr_q[20:16]), .in1(Instr_q[15:11]), .out(multiplexer_2_out), .sel(RegDst));  // open: en
  Multiplexer #(.width(32)) multiplexer_3 (
    .in0(ALUOut_q), .in1(Data_q), .out(multiplexer_3_out), .sel(MemtoReg));  // open: en
  Register_File_main main_2 (
    .Data_Input(multiplexer_3_out), .R_W(R_W), .clock(Clk), .Data_Address(multiplexer_2_out),
    .Selector_A(Instr_q[25:21]), .Selector_B(Instr_q[20:16]), .A(main_2_a), .B(main_2_b));  // open: reset, SOp, PC_enable, High_in, Low_in, Hi_Lo_enable, Stack_Pointer, High_Out, Low_Out
  assign bit_extender_1_out = {{16{Instr_q[15]}}, Instr_q[15:0]};  // Bit_Extender bit_extender_1
  Register #(.width(32)) A (.D(main_2_a), .Q(A_q), .clk(Clk));  // open: en, clr
  Register #(.width(32)) B (.D(main_2_b), .Q(B_q), .clk(Clk));  // open: en, clr
  Shifter #(.width(32)) shifter_1 (.in(bit_extender_1_out), .\dist (5'b00010), .out(shifter_1_out));
  Multiplexer #(.width(32)) multiplexer_4 (
    .in0(main_1_output), .in1(A_q), .out(multiplexer_4_out), .sel(ALUSrcA));  // open: en
  Multiplexer #(.select(2), .width(32)) multiplexer_5 (
    .in0(B_q), .in1(32'h4), .in2(bit_extender_1_out), .in3(shifter_1_out), .out(multiplexer_5_out),
    .sel(ALUSrcB));  // open: en
  // ALU alu_1: pin names not known; wires that end beside it: multiplexer_4_out, multiplexer_5_out, ALUControl, alu_1_p4, alu_1_p5
  and and_1 (and_1_out, Branch, alu_1_p4);
  Register #(.width(32)) ALUOut (.D(alu_1_p5), .Q(ALUOut_q), .clk(Clk));  // open: en, clr
  or or_1 (or_1_out, PCWrite, and_1_out);
  Multiplexer #(.width(32)) multiplexer_6 (
    .in0(alu_1_p5), .in1(ALUOut_q), .out(multiplexer_6_out), .sel(PCSrc));  // open: en

  // Notes on the sheet:
  //   ALU+4
endmodule

module Instruction_Memory (
  input  in_1,
  input  [31:0] in_2,
  input  [31:0] in_3,
  output [31:0] out_4
);
endmodule
